// Logisim project 1.8) Utilisation de multiplexeurs.circ as structural Verilog: 1 circuit, main circuit main
module main (
  input  c,
  input  a0,
  input  a1,
  input  b0,
  input  b1,
  output s0,
  output s1,
  output r
);

  wire not_1_out;
  wire [1:0] adder_1_out, xor_1_out;

  assign xor_1_out = {a1, a0} ^ {b1, b0};  // XOR_Gate xor_1, 2 bits wide
  Adder #(.width(2)) adder_1 (.a({a1, a0}), .b({b1, b0}), .out(adder_1_out), .cout(r));  // open: cin
  Multiplexer #(.width(2), .enable("false")) multiplexer_1 (.in1(xor_1_out), .out({s1, s0}), .sel(c));  // open: in0
  not not_1 (not_1_out, c);
  Multiplexer #(.width(2), .enable("false")) multiplexer_2 (
    .in1(adder_1_out), .out({s1, s0}), .sel(not_1_out));  // open: in0
endmodule
